# Fritzing sketch schematic (saved by Fritzing 0.9.9b)
circuit board: 9.19929cm x 5.82783cm
breadboards: 1

parts:
  M1 = BluePill
  U1 = POT [package=pot_mammoth]
  Connector_to_motor_cable = polarizedheader 4pin 0.156in [package=THT]
  LCD1 = 2.8 Zoll LCD IL19341 [part_number=MSP2807]

nets:
  N1: M1.A6, U1.S
  N2: M1.B0, LCD1.pin4
  N3: M1.3V3, U1.E, LCD1.pin1, LCD1.pin8
  GND: M1.GND, U1.A, Connector_to_motor_cable.pin3, LCD1.pin2
  N4: M1.B12, LCD1.pin3
  N5: M1.B13, LCD1.pin7
  N6: M1.B14, LCD1.pin5
  N7: M1.B15, LCD1.pin6
  N8: M1.A9, Connector_to_motor_cable.pin4
  N9: M1.A10, Connector_to_motor_cable.pin1
  N10: M1.5V, Connector_to_motor_cable.pin2

custom parts:
  BluePill: Generic ebay blue pill STM32F103C8 "Blue pill" CPU module. Arm Cortex M3 128KB flash (usually) 20kb ram, RTC on board. Supported by the Arduino IDE for programming. As cheap as an Arduino nano but with more power and memory.
  2.8 Zoll LCD IL19341: A generic 2.8 inch LCD TFT 320x240 display with touchscreen and SD card slot. Uses the ILI9341 controller, like the Adafruit displays of this size uses.
